# Fritzing sketch bare_bone_arduino (saved by Fritzing 1.0.1rc)
circuit board: 16cm x 10cm
breadboards: 2

parts:
  X2 = USB Connectors [package=usb-b-smt]
  A3 = atmega328 [package=dip]
  C3 = Capacitor [package=cap-pth-small2]
  Y2 = CRYSTAL [package=crystal-smd-10.5x4.8-2pin]
  C4 = Capacitor [package=cap-pth-small2]
  LED1 = LED - 5mm [color="Red (633nm)" current=0.030 package="5 mm [THT]"]
  R1 = Resistor [tolerance=±5% power=0.25 resistance=1000 package=THT]

nets:
  GND: X2.GND, A3.GND, C3.2, C4.2, R1.Pin_1
  N1: X2.VBUS, A3.VCC, A3.AVCC, A3.AREF
  N2: A3.XLAT1, Y2.2, C4.1
  N3: A3.XLAT2, C3.1, Y2.1
  N4: A3.D13, LED1.anode
  N5: LED1.cathode, R1.Pin_0

notes:
  USB
  Capacitors: 22 pF
  Crystal: 16 MHz
  1k Ohm
  Brun svart röd guld
